# Fritzing sketch 코D알고[하]_Ch.3 (saved by Fritzing 0.9.4)
breadboards: 1

parts:
  hc-sr1 = hc-sr04
  LED2 = RGB LED (com. cathode, rgb) [package="5 mm [THT]"]
  R3 = Resistor [tolerance=±5% resistance=470 package="0805 [SMD]"]
  R6 = Resistor [tolerance=±5% resistance=470 package="0805 [SMD]"]
  R7 = Resistor [tolerance=±5% resistance=470 package="0805 [SMD]"]
  부품1 = Arduino Uno (Rev3) - ICSP

nets:
  VCC: hc-sr1.VCC, 부품1.5V
  N1: hc-sr1.Trig, 부품1.D3_PWM
  N2: hc-sr1.Echo, 부품1.D2
  GND: hc-sr1.GND, LED2.common_cathode, 부품1.GND
  N3: LED2.red_anode, R6.Pin_1
  N4: LED2.green_anode, R7.Pin_1
  N5: LED2.blue_anode, R3.Pin_1
  N6: R3.Pin_0, 부품1.D9_PWM
  N7: R6.Pin_0, 부품1.D11_PWM/MOSI
  N8: R7.Pin_0, 부품1.D10_PWM/SS
