# Fritzing sketch 코D알고[하]_Ch.4 (saved by Fritzing 0.9.4)
breadboards: 1

parts:
  부품1 = Arduino Uno (Rev3) - ICSP
  J1 = Piezo Speaker
  hc-sr1 = hc-sr04

nets:
  N1: 부품1.D8, J1.pin2
  N2: 부품1.D12/MISO, hc-sr1.Echo
  N3: 부품1.D13/SCK, hc-sr1.Trig
  5V: 부품1.5V, hc-sr1.VCC
  GND: 부품1.GND, J1.pin1, hc-sr1.GND
