# Fritzing sketch 코D알고[하]_Ch.5 (saved by Fritzing 0.9.4)
breadboards: 1

parts:
  부품1 = Arduino Uno (Rev3) - ICSP
  LED1 = RGB LED (com. cathode, rgb) [package="5 mm [THT]"]
  R1 = Resistor [tolerance=±5% resistance=470 package=THT]
  R2 = Resistor [tolerance=±5% resistance=470 package=THT]
  R3 = Resistor [tolerance=±5% resistance=470 package=THT]

nets:
  N1: 부품1.D2, R1.Pin_0
  N2: 부품1.D3_PWM, R3.Pin_0
  N3: 부품1.D4, R2.Pin_0
  N4: 부품1.GND, LED1.common_cathode
  N5: LED1.red_anode, R2.Pin_1
  N6: LED1.green_anode, R3.Pin_1
  N7: LED1.blue_anode, R1.Pin_1
